# Fritzing sketch Untitled Sketch 4 (saved by Fritzing 0.9.3b)
breadboards: 1

parts:
  U1 = atmega168 [package=dip]
  Part1 = Triple Axis Accelerometer Breakout - ADXL345
  R1 = Resistor [tolerance=±5% resistance=220 package="0402 [SMD]"]
  R2 = Resistor [tolerance=±5% resistance=220 package="0402 [SMD]"]
  C1 = Ceramic Capacitor [capacitance=100nF package="100 mil [THT, multilayer]"]

nets:
  VCC: U1.VCC, Part1.VCC, R1.Pin_1, R2.Pin_1, C1.0
  N1: U1.GND#7, Part1.GND, Part1.CS, Part1.SDO, C1.1
  N2: U1.A4, Part1.SDA, R2.Pin_0
  N3: U1.A5, Part1.SCL, R1.Pin_0

notes:
  Serial Communication
